# Fritzing sketch PonteHComTransistores (saved by Fritzing 0.7.12b)
breadboards: 1

parts:
  Arduino1 = Arduino
  Q1 = NPN-Transistor [package="TO92 [THT]"]
  Q2 = NPN-Transistor [package="TO92 [THT]"]
  Q3 = NPN-Transistor [package="TO92 [THT]"]
  Q4 = NPN-Transistor [package="TO92 [THT]"]
  R1 = Resistor [tolerance=±5% resistance=330 package=THT]
  R2 = Resistor [tolerance=±5% resistance=330 package=THT]
  M1 = DC Motor
  Power_plug1 = Power plug
  R3 = Resistor [tolerance=±5% resistance=330 package=THT]
  R4 = Resistor [tolerance=±5% resistance=330 package=THT]

nets:
  N1: Arduino1.D13, R2.Pin_1
  N2: Arduino1.D12, R1.Pin_1
  N3: Arduino1.D11, R4.Pin_0
  GND: Arduino1.GND, Q1.C, Power_plug1.GND
  N4: Q1.E, R2.Pin_0
  N5: Q1.B, Q3.B, M1.pin_1
  N6: Q2.E, R1.Pin_0
  N7: Q2.B, Q4.B, M1.pin_2
  N8: Q3.E, R3.Pin_1
  N9: Q3.C, Q4.C, Power_plug1.VCC
  N10: Q4.E, R4.Pin_1
