# Fritzing sketch Esquema Controle Motores (saved by Fritzing 0.7.12b)
breadboards: 1

parts:
  IC1 = L293D [package=THT]
  VCC1 = Battery
  D1 = Rectifier Diode [part_number=1N4001 package="300 mil [THT]"]  # not connected
  Arduino1 = Arduino
  IC2 = L293D [package=THT]
  D2 = Rectifier Diode [part_number=1N4001 package="300 mil [THT]"]
  D3 = Rectifier Diode [part_number=1N4001 package="300 mil [THT]"]
  D4 = Rectifier Diode [part_number=1N4001 package="300 mil [THT]"]
  D5 = Rectifier Diode [part_number=1N4001 package="300 mil [THT]"]
  D6 = Rectifier Diode [part_number=1N4001 package="300 mil [THT]"]
  D7 = Rectifier Diode [part_number=1N4001 package="300 mil [THT]"]
  D8 = Rectifier Diode [part_number=1N4001 package="300 mil [THT]"]
  D9 = Rectifier Diode [part_number=1N4001 package="300 mil [THT]"]
  D10 = Rectifier Diode [part_number=1N4001 package="300 mil [THT]"]
  D11 = Rectifier Diode [part_number=1N4001 package="300 mil [THT]"]
  D12 = Rectifier Diode [part_number=1N4001 package="300 mil [THT]"]
  D13 = Rectifier Diode [part_number=1N4001 package="300 mil [THT]"]
  D14 = Rectifier Diode [part_number=1N4001 package="300 mil [THT]"]
  D15 = Rectifier Diode [part_number=1N4001 package="300 mil [THT]"]
  D16 = Rectifier Diode [part_number=1N4001 package="300 mil [THT]"]
  D17 = Rectifier Diode [part_number=1N4001 package="300 mil [THT]"]
  U1 = 74HC595 SMD [package="SO16 [SMD]"]

nets:
  N1: IC1.In_1, U1.Q7
  N2: IC1.Out_1_(_Controlled_by_Enable_1_), D6.cathode, D8.anode
  N3: IC1.0V, VCC1.-, IC2.0V, IC2.+Vmotor, D4.anode, D5.anode, D6.anode, D7.anode, D12.anode, D13.anode, D16.anode, D17.anode, U1.GND, U1.OE
  N4: IC1.Out_2_(_Controlled_by_Enable_1_), D7.cathode, D9.anode
  N5: IC1.In_2, U1.Q0
  N6: IC1.+Vmotor, IC1.+V, IC2.+V, D2.cathode, D3.cathode, D8.cathode, D9.cathode, D10.cathode, D11.cathode, D14.cathode, D15.cathode, U1.MR, U1.VCC
  N7: IC1.In_3, U1.Q6
  N8: IC1.Out_3_(_Controlled_by_Enable_2_), D3.anode, D5.cathode
  N9: IC1.Out_4_(_Controlled_by_Enable_2_), D2.anode, D4.cathode
  N10: IC1.In_4, U1.Q5
  N11: Arduino1.D4, U1.SH_CP
  N12: Arduino1.D3, U1.DS
  N13: Arduino1.D2, U1.ST_CP
  N14: IC2.In_1, U1.Q3
  N15: IC2.Out_1_(_Controlled_by_Enable_1_), D10.anode, D13.cathode
  N16: IC2.Out_2_(_Controlled_by_Enable_1_), D11.anode, D12.cathode
  N17: IC2.In_2, U1.Q4
  N18: IC2.In_3, U1.Q2
  N19: IC2.Out_3_(_Controlled_by_Enable_2_), D14.anode, D16.cathode
  N20: IC2.Out_4_(_Controlled_by_Enable_2_), D15.anode, D17.cathode
  N21: IC2.In_4, U1.Q1
