# Fritzing sketch Esquema Radio Frequência (saved by Fritzing 0.7.12b)

parts:
  U1 = atmega168 [package=dip]
  Arduino1 = Arduino

nets:
  N1: U1.XLAT2, Arduino1.3V3
  N2: U1.D5_(PWM), Arduino1.D8
  N3: U1.D6_(PWM), Arduino1.D13
  N4: U1.D7, Arduino1.D12
  N5: U1.D9_(PWM), Arduino1.GND
  N6: U1.D11_(PWM), Arduino1.D11
  N7: U1.D12, Arduino1.D7
