# Fritzing sketch Esquema Sensor Ultrassonico & Servo (saved by Fritzing 0.7.12b)
breadboards: 1

parts:
  J1 = Basic Servo
  Componente1 = IMU Analog Combo Board - 5 Degrees of Freedom
  Arduino1 = Arduino

nets:
  GND: J1.gnd, Componente1.YOUT, Arduino1.GND
  VCC: J1.vcc, Componente1.XOUT, Arduino1.+5V
  N1: Componente1.ST, Arduino1.D6
  N2: Componente1.YRATE, Arduino1.D5

notes:
  Este componente representa o sensor ultrassonico URM37,
  Sequência de pinos segue da esquerda para direita
  9 8 7 6 5 4 3 2 1
  TXD RXD NC TRIG MOTO PWM nRST GND +5V
